// Digital circuit autofetch.dig as structural Verilog
module autofetch (
  input  CLK,
  input  CLR,
  output OF,
  output [3:0] VAL
);

  wire d_ff_1_q;

  D_FF d_ff_1 (.C(CLK), .Q(d_ff_1_q));  // open: D, nQ
  Counter #(.Bits(4)) counter_1 (.en(d_ff_1_q), .C(CLK), .clr(CLR), .out(VAL), .ovf(OF));
endmodule
